# Fritzing sketch circuit_diagram (saved by Fritzing 1.0.5)

parts:
  Raspberry_Pi_5_(40-pin_header) = Raspberry Pi 3 [part_number=RPI-3-V1.2]
  PCA9685 = PCA9685 16x12-bit PWM Breakout
  Servo_0_(CH0) = Basic Servo
  Servo_1_(CH1) = Basic Servo
  ADS1115 = ADS1115
  MPU6050 = InvenSense MPU6050
  External_5-6V_PSU = BC9VPC [package=bc9vpc]
  Pan_Potentiometer = Rotary Potentiometer (Small) [maximum_resistance=10kΩ knob_status=50% power=0.5W package=THT]
  Tilt_Potentiometer = Rotary Potentiometer (Small) [maximum_resistance=10kΩ knob_status=50% power=0.5W package=THT]
  Servo_2_(CH2) = Basic Servo

nets:
  3V3: Raspberry_Pi_5_(40-pin_header).3v3, PCA9685.no_name_yet#605, ADS1115.VDD, MPU6050.VCC, Pan_Potentiometer.leg1, Tilt_Potentiometer.leg1
  N1: Raspberry_Pi_5_(40-pin_header).GPIO2, PCA9685.no_name_yet#604, ADS1115.SDA, MPU6050.SDA
  N2: Raspberry_Pi_5_(40-pin_header).GPIO3, PCA9685.no_name_yet#603, ADS1115.SCL, MPU6050.SCL
  N3: Raspberry_Pi_5_(40-pin_header).GPIO17, ADS1115.ALRT
  N4: Raspberry_Pi_5_(40-pin_header).GPIO27, MPU6050.INT
  GND: Raspberry_Pi_5_(40-pin_header).GND, PCA9685.no_name_yet#601, PCA9685.no_name_yet#701, PCA9685.no_name_yet#1000, PCA9685.no_name_yet#1001, PCA9685.no_name_yet#1002, Servo_0_(CH0).gnd, Servo_1_(CH1).gnd, ADS1115.GND, MPU6050.GND, External_5-6V_PSU.V-, Pan_Potentiometer.leg2, Tilt_Potentiometer.leg2, Servo_2_(CH2).gnd
  N5: PCA9685.no_name_yet#0, Servo_2_(CH2).pulse
  N6: PCA9685.no_name_yet#1, Servo_1_(CH1).pulse
  N7: PCA9685.no_name_yet#2, Servo_0_(CH0).pulse
  VCC: PCA9685.no_name_yet#100, PCA9685.no_name_yet#101, PCA9685.no_name_yet#102, PCA9685.no_name_yet#706, Servo_0_(CH0).vcc, Servo_1_(CH1).vcc, External_5-6V_PSU.V+, Servo_2_(CH2).vcc
  N8: ADS1115.A0, Tilt_Potentiometer.wiper
  N9: ADS1115.A1, Pan_Potentiometer.wiper

notes:
  I2C Bus (Shared)
  SDA (Pin 3/GPIO2) → PCA9685, ADS1115, MPU6050
  SCL (Pin 5/GPIO3) → PCA9685, ADS1115, MPU6050
  I2C Addresses:
  PCA9685 = 0x40
  ADS1115 = 0x48
  MPU6050 = 0x68
  Interrupts
  GPIO17 (Pin 11) → ADS1115 ALERT/RDY
  GPIO27 (Pin 13) → MPU6050 INT
  Servo Power
  PCA9685 V+ = External 5-6V PSU
  DO NOT power servos from Pi!
  Potentiometers
  Tilt Wiper → ADS1115 A0
  Pan Wiper → ADS1115 A1
  CRITICAL RULES
  • All grounds MUST be connected (common GND)
  • DO NOT swap SDA and SCL
  • DO NOT connect 5-6V to any Pi GPIO
  • PCA9685: VCC=3.3V (logic), V+=5-6V (servos)
  • CSI Camera: ribbon cable to Pi CSI port (no GPIO)

custom parts:
  ADS1115: ADC ADS1115
